# Fritzing sketch Sketch (saved by Fritzing 1.0.1rc)

parts:
  Arduino_CNC_Shield_V3_00_1 = Arduino_CNC_V3.00
  G_|_V_|_X_|_Y_|_B = IC, SIP package, 5 pins [chip_label=JOYSTICK]
  R1 = Resistor [tolerance=±5% power=0.25W resistance=220 package=THT]
  LED1 = LED - 5mm [color="Red (633nm)" current=0.030A package="5 mm [THT]"]
  M2 = Stepper Motor - Bipolar

nets:
  N1: Arduino_CNC_Shield_V3_00_1.EN(able), Arduino_CNC_Shield_V3_00_1.GND#2
  N2: Arduino_CNC_Shield_V3_00_1.X-MTR_'1', M2.A
  N3: Arduino_CNC_Shield_V3_00_1.X-MTR_'2', M2.C
  N4: Arduino_CNC_Shield_V3_00_1.X-MTR_'3', M2.B
  N5: Arduino_CNC_Shield_V3_00_1.X-MTR_'4', M2.D
  N6: Arduino_CNC_Shield_V3_00_1.5V, G_|_V_|_X_|_Y_|_B.pin2
  N7: Arduino_CNC_Shield_V3_00_1.GND#76, G_|_V_|_X_|_Y_|_B.pin1
  N8: Arduino_CNC_Shield_V3_00_1.SpnEn_/_Z_Limit, LED1.anode
  N9: Arduino_CNC_Shield_V3_00_1.SpnDir, G_|_V_|_X_|_Y_|_B.pin5
  N10: Arduino_CNC_Shield_V3_00_1.Abort, G_|_V_|_X_|_Y_|_B.pin3
  N11: Arduino_CNC_Shield_V3_00_1.Hold, G_|_V_|_X_|_Y_|_B.pin4
  N12: Arduino_CNC_Shield_V3_00_1.E-STOP_(Gnd), R1.Pin_1

custom parts:
  Arduino_CNC_V3.00: Protoneer Arduino CNC Shield V3.00 If using Grbl V0.9: The “A” axis can not be used (yet). The “SCL” (Arduino A5) pin is now used for 'Probing' input. The “End Stops Z+ & Z-” (Arduino D11) and “SpnEn” (Arduino D12) have been switched!
